# Fritzing sketch TempMonitorForPE (saved by Fritzing 0.9.3b)
breadboards: 1

parts:
  U1 = NodeMCU V1.0
  WeMos_D1_Mini_OLED_Shield1 = WeMos D1 Mini OLED Shield  # not connected
  S1 = Pushbutton [package="[THT]"]
  DS1 = DS18B20 1-Wire Temperature Sensor [part_number=DS18B20]
  DS2 = DS18B20 1-Wire Temperature Sensor [part_number=DS18B20]
  R1 = Resistor [tolerance=±5% resistance=10k package=THT]
  R2 = Resistor [tolerance=±5% resistance=4.7k package=THT]
  R3 = Resistor [tolerance=±5% resistance=4.7k package=THT]

nets:
  N1: U1.D1, DS1.DQ, R3.Pin_1
  N2: U1.D2, S1.Pin_3, S1.Pin_4, R1.Pin_0
  VDD: U1.3V3, S1.Pin_1, S1.Pin_2, DS1.VDD, DS2.VDD, R3.Pin_0
  GND: U1.GND, DS1.GND, DS2.GND, R1.Pin_1
  N3: U1.D6, DS2.DQ, R2.Pin_1

custom parts:
  NodeMCU V1.0: ESP8266 based NodeMCU
